// Logisim project 7digit.circ as structural Verilog: 1 circuit, main circuit 7digit
module _7digit (
  input  x3,
  input  x2,
  input  x1,
  input  x0,
  output a,
  output b,
  output c,
  output d,
  output e,
  output f,
  output g
);

  wire and_1_out, and_2_out, and_3_out, and_4_out, and_5_out, and_6_out, and_7_out, and_8_out, and_9_out,
       and_10_out, and_11_out, and_12_out, and_13_out, and_14_out, and_15_out, and_16_out, and_17_out,
       and_18_out, and_19_out, and_20_out, not_1_out, not_2_out, not_3_out, not_4_out, not_5_out, not_6_out,
       not_7_out, not_8_out, not_9_out, not_10_out, not_11_out, not_12_out, not_13_out, not_14_out,
       not_15_out, not_16_out, not_17_out, not_18_out, not_19_out, not_20_out, not_21_out, not_22_out,
       not_23_out, not_24_out, not_25_out;

  not not_1 (not_1_out, x2);
  and and_1 (and_1_out, not_1_out, not_2_out);
  not not_2 (not_2_out, x0);
  and and_2 (and_2_out, x2, x0);
  and and_3 (and_3_out, x3, not_3_out);
  not not_3 (not_3_out, x2);
  not not_4 (not_4_out, x2);
  not not_5 (not_5_out, x1);
  and and_4 (and_4_out, not_5_out, not_6_out);
  not not_6 (not_6_out, x0);
  and and_5 (and_5_out, x1, x0);
  not not_7 (not_7_out, x1);
  or or_1 (c, not_7_out, x0, x2);
  not not_8 (not_8_out, x2);
  and and_6 (and_6_out, not_8_out, not_9_out);
  not not_9 (not_9_out, x0);
  not not_10 (not_10_out, x2);
  and and_7 (and_7_out, not_10_out, x1);
  and and_8 (and_8_out, x1, not_11_out);
  not not_11 (not_11_out, x0);
  and and_9 (and_9_out, x2, not_12_out, x0);
  not not_12 (not_12_out, x1);
  and and_10 (and_10_out, x3, not_13_out);
  not not_13 (not_13_out, x2);
  not not_14 (not_14_out, x2);
  and and_11 (and_11_out, not_14_out, not_15_out);
  not not_15 (not_15_out, x0);
  and and_12 (and_12_out, x1, not_16_out);
  not not_16 (not_16_out, x0);
  not not_17 (not_17_out, x1);
  and and_13 (and_13_out, not_17_out, not_18_out);
  not not_18 (not_18_out, x0);
  and and_14 (and_14_out, x2, not_19_out);
  not not_19 (not_19_out, x1);
  and and_15 (and_15_out, x2, not_20_out);
  not not_20 (not_20_out, x0);
  and and_16 (and_16_out, x3, not_21_out);
  not not_21 (not_21_out, x1);
  not not_22 (not_22_out, x2);
  and and_17 (and_17_out, not_22_out, x1);
  and and_18 (and_18_out, x2, not_23_out);
  not not_23 (not_23_out, x1);
  and and_19 (and_19_out, x2, not_24_out);
  not not_24 (not_24_out, x0);
  and and_20 (and_20_out, x3, not_25_out);
  not not_25 (not_25_out, x2);
  or or_2 (a, and_1_out, x1, and_2_out, and_3_out);
  or or_3 (b, not_4_out, and_4_out, and_5_out);
  or or_4 (d, and_6_out, and_7_out, and_8_out, and_9_out, and_10_out);
  or or_5 (e, and_11_out, and_12_out);
  or or_6 (f, and_13_out, and_14_out, and_15_out, and_16_out);
  or or_7 (g, and_17_out, and_18_out, and_19_out, and_20_out);
endmodule
