// Logisim project main_POTEC_project.circ as structural Verilog: 1 circuit, main circuit main
module main (
  input  [3:0] in_1
);

  wire n7digit_1_a, n7digit_1_b, n7digit_1_c, n7digit_1_d, n7digit_1_e, n7digit_1_f, n7digit_1_g, not_1_out,
       not_2_out, not_3_out, not_4_out, not_5_out, not_6_out, not_7_out;

  _7digit u_7digit_1 (
    .x3(in_1[3]), .x2(in_1[2]), .x1(in_1[1]), .x0(in_1[0]), .a(n7digit_1_a), .b(n7digit_1_b),
    .c(n7digit_1_c), .d(n7digit_1_d), .e(n7digit_1_e), .f(n7digit_1_f), .g(n7digit_1_g));
  not not_1 (not_1_out, n7digit_1_a);
  not not_2 (not_2_out, n7digit_1_b);
  not not_3 (not_3_out, n7digit_1_f);
  not not_4 (not_4_out, n7digit_1_g);
  _7_Segment_Display u_7_segment_display_1 (
    .g(not_4_out), .f(not_3_out), .a(not_1_out), .b(not_2_out), .e(not_5_out), .d(not_6_out), .c(not_7_out));  // open: dp
  not not_5 (not_5_out, n7digit_1_e);
  not not_6 (not_6_out, n7digit_1_d);
  not not_7 (not_7_out, n7digit_1_c);
endmodule
